# Fritzing sketch LightSwitch (saved by Fritzing 0.8.7b)
breadboards: 1

parts:
  R1 = Resistor [tolerance=±5% resistance=330 package=THT]
  Part1 = Arduino Uno (Rev3)
  LED1 = smd LED [color="Green (555nm)" package="1206 [SMD]"]
  R2 = Resistor [tolerance=±5% resistance=330 package=THT]
  LED2 = smd LED [color="Yellow (585nm)" package="1206 [SMD]"]
  R3 = Resistor [tolerance=±5% resistance=330 package=THT]
  LED3 = smd LED [color="Red (633nm)" package="1206 [SMD]"]  # not connected
  S1 = Pushbutton [package="[THT]"]

nets:
  N1: R1.Pin_0, LED1.anode
  N2: R1.Pin_1, Part1.D2
  N3: Part1.A5/SCL, S1.Pin_1, S1.Pin_2
  N4: Part1.D3_PWM, R2.Pin_1
  N5: Part1.D4, R3.Pin_1
  N6: Part1.GND, LED1.cathode, LED2.cathode, S1.Pin_3, S1.Pin_4
  N7: R2.Pin_0, LED2.anode
